# Fritzing sketch anemometer (saved by Fritzing 0.9.3b)

parts:
  U1 = NodeMCU V3.0
  M1 = DC Motor
  R1 = Resistor [tolerance=±5% resistance=10k package=THT]

nets:
  N1: U1.D1, M1.pin_1, R1.Pin_1
  N2: U1.3V3, M1.pin_2
  N3: U1.GND, R1.Pin_0

custom parts:
  NodeMCU V3.0: ESP8266 based NodeMCU
