# Fritzing sketch rainfall-sensor-testing (saved by Fritzing 0.9.3b)

parts:
  U3 = NodeMCU V3.0
  YL-83_-_Detection_Board1 = YL-83 Rain Sensor - Detection Board
  YL-83_-_Control_Board1 = YL-83 Rain Sensor - Control Board

nets:
  3V3: U3.3V3, YL-83_-_Control_Board1.VCC
  GND: U3.GND, YL-83_-_Control_Board1.GND
  N1: U3.A0, YL-83_-_Control_Board1.AO
  N2: YL-83_-_Detection_Board1.POS, YL-83_-_Control_Board1.POS
  N3: YL-83_-_Detection_Board1.NEG, YL-83_-_Control_Board1.NEG

custom parts:
  NodeMCU V3.0: ESP8266 based NodeMCU
  YL-83 Rain Sensor - Detection Board: The YL-83 is a rain sensor that has more resistance when dry and less resistance when wet. The module runs at 5V.
  YL-83 Rain Sensor - Control Board: The YL-83 is a rain sensor that has more resistance when dry and less resistance when wet. The module runs at 5V.
