# Fritzing sketch uv-sensor-testing (saved by Fritzing 0.9.3b)

parts:
  U2 = NodeMCU V3.0
  UV_Sensor1 = ML8511 UV Sensor Breakout [part_number=SEN-12705]

nets:
  3V3: U2.3V3, U2.D5, UV_Sensor1.EN, UV_Sensor1.3.3V
  GND: U2.GND, UV_Sensor1.GND
  N1: U2.A0, UV_Sensor1.OUT

custom parts:
  NodeMCU V3.0: ESP8266 based NodeMCU
  ML8511 UV Sensor Breakout: Description: The ML8511 breakout is an easy to use ultraviolet light sensor. The MP8511 UV Sensor works by outputing an analog signal in relation to the amount of UV light it detects. This breakout can be very handy in creating devices that warn the user of sunburn or detect the UV index as it relates to weather conditions. This sensor breakout can detect 280-390nm light most effectively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
