# Fritzing sketch weather-station (saved by Fritzing 0.9.3b)

parts:
  U1 = NodeMCU V3.0
  BME280_Temp_/_Humidity_/_Air_Pressure = BME280 Breakout
  Mod2 = SDS011 - dust sensor [part_number=1]
  Rainfall_Detector = YL-83 Rain Sensor - Detection Board
  Rainfall_Adapter = YL-83 Rain Sensor - Control Board
  UV_Sensor = ML8511 UV Sensor Breakout [part_number=SEN-12705]
  Anemometer = DC Motor
  R2 = Resistor [tolerance=±5% resistance=10k package=THT]

nets:
  N1: U1.D0, UV_Sensor.OUT
  N2: U1.D1, BME280_Temp_/_Humidity_/_Air_Pressure.SCK/SCL
  N3: U1.D2, BME280_Temp_/_Humidity_/_Air_Pressure.SDI/SDA
  N4: U1.D3, Mod2.RXD
  N5: U1.D4, Mod2.TXD
  3.3V: U1.3V3, BME280_Temp_/_Humidity_/_Air_Pressure.3.3V, Rainfall_Adapter.VCC, UV_Sensor.3.3V, Anemometer.pin_1
  GND: U1.GND#6, U1.GND#13, U1.GND#16, U1.GND#33, BME280_Temp_/_Humidity_/_Air_Pressure.GND, Rainfall_Adapter.GND, UV_Sensor.GND, R2.Pin_1
  N6: U1.D6, Rainfall_Adapter.AO
  N7: U1.D7, Anemometer.pin_2, R2.Pin_0
  N8: U1.VU, Mod2.5V
  N9: U1.GND#41, Mod2.GND
  N10: Rainfall_Detector.POS, Rainfall_Adapter.POS
  N11: Rainfall_Detector.NEG, Rainfall_Adapter.NEG

custom parts:
  NodeMCU V3.0: ESP8266 based NodeMCU
  SDS011 - dust sensor: The SDS 011 Sensor is a quite recent Air Quality Sensor developed by inovafit, a spin-off from the university of Jinan (in Shandong). With its size, it is probably one of the best sensor in terms of accuracy: While other sensors tend to focus on shrinking the sensor size, the SDS 011 has opted for a size tradeoff allowing it to use a larger fan. And the larger the fan, the better the quality.
  YL-83 Rain Sensor - Detection Board: The YL-83 is a rain sensor that has more resistance when dry and less resistance when wet. The module runs at 5V.
  YL-83 Rain Sensor - Control Board: The YL-83 is a rain sensor that has more resistance when dry and less resistance when wet. The module runs at 5V.
  ML8511 UV Sensor Breakout: Description: The ML8511 breakout is an easy to use ultraviolet light sensor. The MP8511 UV Sensor works by outputing an analog signal in relation to the amount of UV light it detects. This breakout can be very handy in creating devices that warn the user of sunburn or detect the UV index as it relates to weather conditions. This sensor breakout can detect 280-390nm light most effectively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
